# Fritzing sketch smart farm (saved by Fritzing 0.8.7b)
breadboards: 1

parts:
  U1 = 4-Channel 5v Relay Shield [package=relay-4ch5v10a]
  WATER_PUMP1 = water pump/motor  # not connected
  PS1 = prefix0000 [part_number=S-350-60]  # not connected
  U3 = ESP32-38PinWide [part_number=ESP32-38PinWide]
  LPD8806_RGB_LED_Strip1 = LPD8806 RGB LED Strip
  YF-S201_Flow_Meter1 = YF-S201 Water Flow Meter

nets:
  GND: U1.GND, U3.GND, LPD8806_RGB_LED_Strip1.GND
  N1: U1.IN1, U3.GPIO25
  N2: U1.IN2, U3.GPIO26
  N3: U1.K1-Off, U3.VIN
  N4: U1.K1-On, YF-S201_Flow_Meter1.VCC
  N5: U1.K2-On, LPD8806_RGB_LED_Strip1.CI

notes:
  dcdc
  12v (+)----------------
  12 (-)------------------
  5v (+)
  5v (-)
  3v (+)
  3v (-)
  power adapter (+)
  power adapter (-)
  220 (+)
  220 (-)
  220 gnd

custom parts:
  4-Channel 5v Relay Shield: 4 Channel 5v Relay Shield w. 2x SPD-06VDC-SD-C
  water pump/motor: WATER PUMP BY ARDUBLOCKTR
  ESP32-38PinWide: Generic 38-Pin ESP32 with wide format (only access to one side of pins on a breadboard) based on Stephen Lilley's HiLetgo ESP-WROOM-32 ESP32 ESP-32S Development Board.
  LPD8806 RGB LED Strip: Digitally addressable RGB LED strip
  YF-S201 Water Flow Meter: The YF-S201 Flow Meter. The input voltage is 5V to 24V (DC).
